// Logisim project LAB_2_AC.circ as structural Verilog: 1 circuit, main circuit main
module main (
  input  X,
  input  Y,
  input  X_2,
  input  Y_2,
  input  in_5,
  input  D0,
  input  S,
  input  D1,
  input  in_9,
  output F_X_Y,
  output out_11,
  output out_12,
  output out_13,
  output Y_3
);

  wire and_1_out, and_2_out, button_1_out, button_2_out, clock_1_out, d_ff_2_qn, d_ff_3_q, d_ff_3_qn,
       d_ff_4_q, d_ff_4_qn, demultiplexer_1_out0, demultiplexer_1_out1, not_1_out;

  Button button_1 (.out(button_1_out));
  Button button_2 (.out(button_2_out));
  Clock clock_1 (.out(clock_1_out));
  or or_1 (F_X_Y, X, Y);
  xnor xnor_1 (out_11, X_2, Y_2);
  D_Flip_Flop d_ff_1 (.clk(clock_1_out), .D(in_5), .Q(out_12), .Qn(out_13));  // open: preset, en, reset
  not not_1 (not_1_out, S);
  D_Flip_Flop d_ff_2 (.clk(button_1_out), .D(d_ff_4_qn), .Qn(d_ff_2_qn));  // open: Q, preset, en, reset
  D_Flip_Flop d_ff_3 (.clk(button_2_out), .D(d_ff_3_qn), .Q(d_ff_3_q), .Qn(d_ff_3_qn));  // open: preset, en, reset
  and and_1 (and_1_out, D0, not_1_out);
  and and_2 (and_2_out, S, D1);
  D_Flip_Flop d_ff_4 (.clk(button_1_out), .D(d_ff_2_qn), .Q(d_ff_4_q), .Qn(d_ff_4_qn));  // open: preset, en, reset
  or or_2 (Y_3, and_1_out, and_2_out);
  Demultiplexer demultiplexer_1 (
    .out0(demultiplexer_1_out0), .out1(demultiplexer_1_out1), .in(in_9), .sel(d_ff_4_q));  // open: en
  LED led_1 (.in(d_ff_3_q));
  LED led_2 (.in(d_ff_3_qn));
  LED led_3 (.in(demultiplexer_1_out0));
  LED led_4 (.in(demultiplexer_1_out1));

  // Notes on the sheet:
  //   XNOR Gate
  //   2-to-1 MUX
  //   Or Gate
  //   D Flip Flop
  //   2 leds 1 button
endmodule
