// Logisim project alab3.circ as structural Verilog: 30 circuits, main circuit Ex1E
module Ex1E (
  input  A,
  input  B,
  output F
);

  wire nand_1_out, nand_2_out, nand_3_out;

  nand nand_1 (nand_1_out, A, B);
  nand nand_2 (nand_2_out, A, nand_1_out);
  nand nand_3 (nand_3_out, nand_1_out, B);
  nand nand_4 (F, nand_2_out, nand_3_out);

  // Notes on the sheet:
  //   LAB 3 AC
  //   Ex 1E
endmodule

module Ex2E (
  input  A,
  input  B,
  output F
);

  wire nor_1_out, nor_2_out, nor_3_out;

  nor nor_1 (nor_1_out, A, B);
  nor nor_2 (nor_2_out, A, nor_1_out);
  nor nor_3 (nor_3_out, nor_1_out, B);
  nor nor_4 (F, nor_2_out, nor_3_out);

  // Notes on the sheet:
  //   Exercitiul 2E
endmodule

module Ex5E (
  input  A,
  output Y_prime
);

  nand nand_1 (Y_prime, A, A);
endmodule

module Ex2M (
  input  A,
  input  B,
  output Y
);

  or or_1 (Y, A, B);

  // Notes on the sheet:
  //   Ex2M
endmodule

module Ex1M (
  input  A,
  input  B,
  output Y
);

  xnor xnor_1 (Y, A, B);

  // Notes on the sheet:
  //   Ex1M
endmodule

module Ex3M (
  input  A,
  input  B,
  output Y
);

  xor xor_1 (Y, A, B);
endmodule

module Ex6M (
  input  A,
  input  B,
  output Y
);

  nor nor_1 (Y, A, B);
endmodule

module Ex7M (
  input  A,
  input  B,
  output Y
);

  and and_1 (Y, A, B);
endmodule

module Ex14M (
  input  A,
  input  B,
  output Y
);

  xnor xnor_1 (Y, A, B);
endmodule

module Ex13M (
  input  A,
  input  B,
  output out_3
);

  nand nand_1 (out_3, A, B);
endmodule

module Ex2H (
  input  in_1,
  input  in_2,
  input  in_3,
  input  in_4,
  input  in_5,
  input  [3:0] in_6,
  output out_7,
  output out_8,
  output out_9,
  output out_10,
  output out_11,
  output out_12,
  output out_13,
  output out_14,
  output out_15,
  output out_16,
  output out_17,
  output out_18,
  output out_19,
  output out_20,
  output out_21,
  output out_22,
  output out_23,
  output out_24,
  output out_25,
  output out_26,
  output out_27,
  output out_28,
  output out_29,
  output out_30,
  output out_31,
  output out_32,
  output out_33,
  output out_34,
  output out_35,
  output out_36,
  output out_37,
  output out_38
);

  wire not_1_out, not_2_out, not_3_out, not_4_out;

  Decoder #(.select(4)) decoder_1 (
    .out0(out_7), .out1(out_8), .out2(out_8), .out3(out_10), .out4(out_11), .out5(out_12), .out6(out_14),
    .out7(out_15), .out8(out_16), .out9(out_18), .out10(out_19), .out11(out_20), .out12(out_22),
    .out13(out_23), .out14(out_24), .out15(out_26), .sel(in_6), .en(in_5));
  not not_1 (not_1_out, in_1);
  not not_2 (not_2_out, in_2);
  not not_3 (not_3_out, in_3);
  not not_4 (not_4_out, in_4);
  and q1 (out_13, not_4_out, not_3_out, not_2_out, not_1_out);
  and q2 (out_17, in_4, not_3_out, not_2_out, not_1_out);
  and q3 (out_21, not_4_out, in_3, not_2_out, not_1_out);
  and q4 (out_25, in_4, in_3, not_2_out, not_1_out);
  and q5 (out_27, not_4_out, not_3_out, in_2, not_1_out);
  and q6 (out_28, in_4, not_3_out, in_2, not_1_out);
  and q7 (out_29, not_4_out, in_3, in_2, not_1_out);
  and q8 (out_30, in_4, in_3, in_2, not_1_out);
  and q9 (out_31, not_4_out, not_3_out, not_2_out, in_1);
  and q10 (out_32, in_4, not_3_out, not_2_out, in_1);
  and q11 (out_33, not_4_out, in_3, not_2_out, in_1);
  and q12 (out_34, in_4, in_3, not_2_out, in_1);
  and q13 (out_35, not_4_out, not_3_out, in_2, in_1);
  and q14 (out_36, in_4, not_3_out, in_2, in_1);
  and q15 (out_37, not_4_out, in_3, in_2, in_1);
  and q16 (out_38, in_4, in_3, in_2, in_1);

  assign out_9 = out_8;
endmodule

module Ex4M (
  input  A,
  input  B,
  output F
);

  xor xor_1 (F, A, B);
  LED led_1 (.in(F));

  // Notes on the sheet:
  //   va activa iesirea daca una dintre doua intrari este 1 si cealalta este 0
endmodule

module Ex5M (
  input  in_1,
  input  in_2,
  input  A,
  input  B,
  output out_5,
  output Y
);

  wire nor_1_out, nor_2_out, nor_3_out, nor_4_out;

  xor xor_1 (out_5, in_1, in_2);
  nor nor_1 (nor_1_out, A, B);
  nor nor_2 (nor_2_out, A, nor_1_out);
  nor nor_3 (nor_3_out, nor_1_out, B);
  nor nor_4 (nor_4_out, nor_2_out, nor_3_out);
  nor nor_5 (Y, nor_4_out, nor_4_out);

  // Notes on the sheet:
  //   va activa iesirea daca una dintre  intrari este 1 si cealalta 0
endmodule

module Ex18M (
  input  A,
  input  B,
  output Y
);

  wire nor_1_out, nor_2_out, nor_3_out;

  nor nor_1 (nor_1_out, A, B);
  nor nor_2 (nor_2_out, A, nor_1_out);
  nor nor_3 (nor_3_out, nor_1_out, B);
  nor nor_4 (Y, nor_2_out, nor_3_out);

  // Notes on the sheet:
  //   Xnor gate 
endmodule

module Ex9M (
  input  A,
  output Y
);

  not not_1 (Y, A);
endmodule

module Ex10M (
  input  A,
  output Y
);

  wire not_1_out;

  not not_1 (not_1_out, A);
  not not_2 (Y, not_1_out);
endmodule

module Ex1H (
  input  A3,
  input  B3,
  input  A2,
  input  B2,
  input  A1,
  input  B1,
  input  A0,
  input  B0,
  input  [3:0] A,
  input  [3:0] B,
  output A_B,
  output A_B_2,
  output A_B_3,
  output A_B_4,
  output A_B_5,
  output A_B_6
);

  wire and_1_out, and_2_out, and_3_out, and_4_out, and_5_out, and_6_out, and_7_out, and_8_out, and_9_out,
       and_10_out, and_11_out, and_12_out, and_13_out, and_14_out, not_1_out, not_2_out, not_3_out,
       not_4_out, not_5_out, not_6_out, not_7_out, not_8_out, x0_out, x1_out, x2_out, x3_out;

  not not_1 (not_1_out, A3);
  not not_2 (not_2_out, B3);
  not not_3 (not_3_out, A2);
  not not_4 (not_4_out, B2);
  not not_5 (not_5_out, A1);
  not not_6 (not_6_out, B1);
  not not_7 (not_7_out, A0);
  not not_8 (not_8_out, B0);
  Comparator #(.width(4)) comparator_1 (.a(A), .b(B), .gt(A_B_4), .eq(A_B_5), .lt(A_B_6));
  and and_1 (and_1_out, not_1_out, B3);
  and and_2 (and_2_out, A3, not_2_out);
  and and_3 (and_3_out, not_3_out, B2);
  and and_4 (and_4_out, A2, not_4_out);
  and and_5 (and_5_out, not_5_out, B1);
  and and_6 (and_6_out, A1, not_6_out);
  and and_7 (and_7_out, not_7_out, B0);
  and and_8 (and_8_out, A0, not_8_out);
  nor x3 (x3_out, and_1_out, and_2_out);
  nor x2 (x2_out, and_3_out, and_4_out);
  nor x1 (x1_out, and_5_out, and_6_out);
  nor x0 (x0_out, and_7_out, and_8_out);
  and and_9 (and_9_out, x3_out, and_3_out);
  and and_10 (and_10_out, x3_out, and_4_out);
  and and_11 (and_11_out, x3_out, x2_out, and_5_out);
  and and_12 (and_12_out, x3_out, x2_out, and_6_out);
  and and_13 (and_13_out, x3_out, x2_out, and_7_out);
  and and_14 (and_14_out, x3_out, x2_out, x1_out, and_8_out);
  and and_15 (A_B_3, x3_out, x2_out, x1_out, x0_out);
  or or_1 (A_B, and_1_out, and_9_out, and_11_out, and_13_out);
  or or_2 (A_B_2, and_2_out, and_10_out, and_12_out, and_14_out);
endmodule

module Ex11M (
  input  A,
  input  B,
  output Y
);

  wire nand_1_out;

  nand nand_1 (nand_1_out, A, B);
  nand nand_2 (Y, nand_1_out, nand_1_out);

  // Notes on the sheet:
  //   and gate
endmodule

module Ex12M (
  input  A,
  input  B,
  output F
);

  wire nand_1_out, nand_2_out;

  nand nand_1 (nand_1_out, A, A);
  nand nand_2 (nand_2_out, B, B);
  nand nand_3 (F, nand_1_out, nand_2_out);

  // Notes on the sheet:
  //   or gate
endmodule

module Ex16M (
  input  A,
  input  B,
  output Y
);

  xnor xnor_1 (Y, A, B);
endmodule

module Ex4H (
  input  in_1,
  input  [7:0] First_Term,
  input  [7:0] Second_Term,
  input  [7:0] in_4,
  input  [7:0] in_5,
  output out_6,
  output [7:0] The_Result
);

  Adder adder_1 (.a(First_Term), .b(Second_Term), .out(The_Result), .cin(in_1), .cout(out_6));

  // Notes on the sheet:
  //   nu e corect
endmodule

module Ex11H (
  input  [7:0] in_1,
  input  [7:0] in_2,
  output [7:0] out_3,
  output [7:0] out_4
);

  Negator negator_1 (.in(in_1), .out(out_3));
  assign out_4 = ~in_2;  // NOT_Gate not_1, 8 bits wide

  // Notes on the sheet:
  //   gresit
endmodule

module Ex5H (
  input  in_1,
  input  [7:0] First_Term,
  input  [7:0] Second_Term,
  output [7:0] out_4,
  output [7:0] out_5
);

  wire [7:0] undriven;

  Multiplier multiplier_1 (.a(First_Term), .b(Second_Term), .out(out_5), .cin(undriven), .cout(out_4));

  // Notes on the sheet:
  //   The Result
endmodule

module Ex6H (
  input  [7:0] in_1,
  input  [7:0] First_Term,
  input  [7:0] Second_Term,
  output [7:0] Result,
  output [7:0] Remainder
);

  Divider divider_1 (.a(First_Term), .b(Second_Term), .out(Result), .upper(in_1), .rem(Remainder));
endmodule

module Ex15M (
  input  A,
  input  B,
  output Y
);

  or or_1 (Y, A, B);
endmodule

module Ex17M (
  input  A,
  input  B,
  output Y
);

  nand nand_1 (Y, A, B);
endmodule

module Ex19M (
  input  A,
  input  B,
  output Y
);

  and and_1 (Y, A, B);
endmodule

module Ex8M (
  input  A,
  output F
);

  not not_1 (F, A);
endmodule

module Ex6E (
  input  in_1,
  input  in_2,
  output out_3
);

  wire nor_1_out, nor_2_out;

  nor nor_1 (nor_1_out, in_1, in_1);
  nor nor_2 (nor_2_out, in_2, in_2);
  nor nor_3 (out_3, nor_1_out, nor_2_out);
endmodule

module Ex10E (
  input  in_1,
  input  in_2,
  input  in_3,
  input  in_4,
  output out_5
);

  wire nand_1_out, nand_2_out, nand_3_out, nand_4_out, nand_5_out;

  nand nand_1 (nand_1_out, in_1, in_2);
  nand nand_2 (nand_2_out, in_3, in_4);
  nand nand_3 (nand_3_out, nand_1_out, nand_1_out);
  nand nand_4 (nand_4_out, nand_2_out, nand_2_out);
  nand nand_5 (nand_5_out, nand_3_out, nand_4_out);
  nand nand_6 (out_5, nand_5_out, nand_5_out);
endmodule
